# Fritzing sketch schematic (saved by Fritzing 0.9.3b)
breadboards: 1

parts:
  Power_plug1 = Power plug
  M1 = DC Motor
  LCD1 = LCD screen
  R1 = Resistor [tolerance=±5% resistance=220 package=THT]
  R2 = Rotary Potentiometer (Small) [maximum_resistance=100kΩ package=THT]
  Fuse1 = Fuse with Handler [part_number=Htc-15m]
  Q1 = Basic FET N-Channel [package="TO220 [THT]"]
  Part1 = Arduino Uno (Rev3)
  Part2 = Adafruit SGP30 [part_number="Adafruit #3709"]
  J1 = Piezo Speaker
  U1 = Voltage Regulator - 5V [package="TO220 [THT]"]
  R3 = Resistor [tolerance=±5% resistance=220 package=THT]

nets:
  GND: Power_plug1.GND, M1.pin_2, Part1.GND, Part2.GND, U1.GND, R3.Pin_1
  N1: Power_plug1.VCC, Fuse1.Connector1
  N2: M1.pin_1, Q1.source
  N3: LCD1.VSS, R2.leg1
  N4: LCD1.VDD, LCD1.LED-, R1.Pin_0, R2.leg2, U1.output_voltage
  N5: LCD1.V0, R2.wiper
  N6: LCD1.LED+, R1.Pin_1
  N7: Fuse1.Connector2, Q1.drain, U1.input_voltage
  N8: Q1.gate, Part1.D8
  N9: Part1.D12/MISO, J1.pin2
  N10: Part1.A4/SDA, Part2.SDA
  N11: Part1.A5/SCL, Part2.SCL
  3V3: Part1.3V3, Part2.VCC
  N12: J1.pin1, R3.Pin_0

custom parts:
  Adafruit SGP30: Breathe easy with the SGP30 Multi-Pixel Gas Sensor, a fully integrated MOX gas sensor. This is a very fine air quality sensor from the sensor experts at Sensirion, with I2C interfacing and fully calibrated output signals with a typical accuracy of 15% within measured values. The SGP combines multiple metal-oxide sensing elements on one chip to provide more detailed air quality signals. This is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
